// Logisim project 16Bit_CPU.circ as structural Verilog
module RegisterFile (
  input  [2:0] RB,
  input  [2:0] RA,
  input  [2:0] RW,
  input  RegWrite,
  input  [15:0] BusW,
  output [15:0] BusA,
  output [15:0] BusB
);

  wire and_1_out, and_2_out, and_3_out, and_4_out, and_5_out, and_6_out, and_7_out, clock_1_out,
       decoder_1_out1, decoder_1_out2, decoder_1_out3, decoder_1_out4, decoder_1_out5, decoder_1_out6,
       decoder_1_out7, decoder_2_out0, decoder_2_out1, decoder_2_out2, decoder_2_out3, decoder_2_out4,
       decoder_2_out5, decoder_2_out6, decoder_2_out7, decoder_3_out0, decoder_3_out1, decoder_3_out2,
       decoder_3_out3, decoder_3_out4, decoder_3_out5, decoder_3_out6, decoder_3_out7, undriven;
  wire [15:0] R1_q, R2_q, R3_q, R4_q, R5_q, R6_q, R7_q;

  Decoder #(.enable("false"), .select(3)) decoder_1 (
    .out1(decoder_1_out1), .out2(decoder_1_out2), .out3(decoder_1_out3), .out4(decoder_1_out4),
    .out5(decoder_1_out5), .out6(decoder_1_out6), .out7(decoder_1_out7), .sel(RW));  // open: out0
  Clock clock_1 (.out(clock_1_out));
  and and_1 (and_1_out, decoder_1_out1, RegWrite);
  and and_2 (and_2_out, decoder_1_out2, RegWrite);
  and and_3 (and_3_out, decoder_1_out3, RegWrite);
  and and_4 (and_4_out, decoder_1_out4, RegWrite);
  and and_5 (and_5_out, decoder_1_out5, RegWrite);
  and and_6 (and_6_out, decoder_1_out6, RegWrite);
  and and_7 (and_7_out, decoder_1_out7, RegWrite);
  Register #(.width(16)) R1 (.D(BusW), .en(and_1_out), .clk(clock_1_out), .Q(R1_q));  // open: clr
  Register #(.width(16)) R2 (.D(BusW), .en(and_2_out), .clk(clock_1_out), .Q(R2_q));  // open: clr
  Register #(.width(16)) R3 (.D(BusW), .en(and_3_out), .clk(clock_1_out), .Q(R3_q));  // open: clr
  Register #(.width(16)) R4 (.D(BusW), .en(and_4_out), .clk(clock_1_out), .Q(R4_q));  // open: clr
  Register #(.width(16)) R5 (.D(BusW), .en(and_5_out), .clk(clock_1_out), .Q(R5_q));  // open: clr
  Register #(.width(16)) R6 (.D(BusW), .en(and_6_out), .clk(clock_1_out), .Q(R6_q));  // open: clr
  Register #(.width(16)) R7 (.D(BusW), .en(and_7_out), .clk(clock_1_out), .Q(R7_q));  // open: clr
  assign BusA = decoder_2_out1 ? R1_q : 16'bz;  // Controlled_Buffer controlled_buffer_1
  assign BusA = decoder_2_out2 ? R2_q : 16'bz;  // Controlled_Buffer controlled_buffer_2
  assign BusA = decoder_2_out3 ? R3_q : 16'bz;  // Controlled_Buffer controlled_buffer_3
  assign BusA = decoder_2_out4 ? R4_q : 16'bz;  // Controlled_Buffer controlled_buffer_4
  assign BusA = decoder_2_out5 ? R5_q : 16'bz;  // Controlled_Buffer controlled_buffer_5
  assign BusA = decoder_2_out6 ? R6_q : 16'bz;  // Controlled_Buffer controlled_buffer_6
  assign BusA = decoder_2_out7 ? R7_q : 16'bz;  // Controlled_Buffer controlled_buffer_7
  Decoder #(.enable("false"), .select(3)) decoder_2 (
    .out0(decoder_2_out0), .out1(decoder_2_out1), .out2(decoder_2_out2), .out3(decoder_2_out3),
    .out4(decoder_2_out4), .out5(decoder_2_out5), .out6(decoder_2_out6), .out7(decoder_2_out7), .sel(RA));
  assign BusA = decoder_2_out0 ? {16{1'b0}} : 16'bz;  // Controlled_Buffer controlled_buffer_8
  assign BusB = decoder_3_out1 ? R1_q : 16'bz;  // Controlled_Buffer controlled_buffer_9
  assign BusB = decoder_3_out2 ? R2_q : 16'bz;  // Controlled_Buffer controlled_buffer_10
  assign BusB = decoder_3_out3 ? R3_q : 16'bz;  // Controlled_Buffer controlled_buffer_11
  assign BusB = decoder_3_out4 ? R4_q : 16'bz;  // Controlled_Buffer controlled_buffer_12
  assign BusB = decoder_3_out5 ? R5_q : 16'bz;  // Controlled_Buffer controlled_buffer_13
  assign BusB = decoder_3_out6 ? R6_q : 16'bz;  // Controlled_Buffer controlled_buffer_14
  assign BusB = undriven ? R7_q : 16'bz;  // Controlled_Buffer controlled_buffer_15
  Decoder #(.enable("false"), .select(3)) decoder_3 (
    .out0(decoder_3_out0), .out1(decoder_3_out1), .out2(decoder_3_out2), .out3(decoder_3_out3),
    .out4(decoder_3_out4), .out5(decoder_3_out5), .out6(decoder_3_out6), .out7(decoder_3_out7), .sel(RB));
  assign BusB = decoder_3_out0 ? {16{1'b0}} : 16'bz;  // Controlled_Buffer controlled_buffer_16
endmodule

module Main_CPU (
);

  wire ALUSrc, CrtlRE, CrtlWE, ExtOp, RegDst, RegWr, WBdata, Zero;
  wire [1:0] ALUFun, f;
  wire [2:0] ALUOP, multiplexer_3_out, spliter_1_rd, spliter_1_rs, spliter_1_rt;
  wire [4:0] imm5, OpCode;
  wire [10:0] imm11;
  wire [15:0] adder_2_out, adder_3_out, Address, ALUResult, BusW, DataIn, Ext_imm5, Ext_imm11,
       multiplexer_1_out, multiplexer_2_out, multiplexer_4_out, PC_PLUS_1, pcpro_1_q, ram_1_dout,
       registerfile_1_busb, rom_1_data;
  wire [15:1] alu_circit_1_zero;

  PCPro pcpro_1 (.D(multiplexer_1_out), .Q(pcpro_1_q));  // open: PCRst
  Multiplexer #(.select(2), .width(16)) multiplexer_1 (
    .in0(multiplexer_2_out), .in1(adder_2_out), .in2(PC_PLUS_1), .out(multiplexer_1_out));  // open: in3, sel
  Adder #(.width(16)) adder_1 (.a(16'h1), .b(pcpro_1_q), .out(PC_PLUS_1));  // open: cin, cout
  ROM #(.addrWidth(16), .dataWidth(16)) rom_1 (.addr(pcpro_1_q), .data(rom_1_data));
  Adder #(.width(16)) adder_2 (.a(pcpro_1_q), .b(Ext_imm11), .out(adder_2_out));  // open: cin, cout
  Adder #(.width(16)) adder_3 (.a(pcpro_1_q), .b(Ext_imm5), .out(adder_3_out));  // open: cin, cout
  Multiplexer #(.width(16)) multiplexer_2 (.in0(PC_PLUS_1), .in1(adder_3_out), .out(multiplexer_2_out), .sel(Zero));
  Spliter spliter_1 (
    .I(rom_1_data), .imm11(imm11), .Rt(spliter_1_rt), .Rs(spliter_1_rs), .Rd(spliter_1_rd), .f(f),
    .OpCode(OpCode), .imm5(imm5));
  Multiplexer #(.width(3)) multiplexer_3 (
    .in0(spliter_1_rt), .in1(spliter_1_rd), .out(multiplexer_3_out), .sel(RegDst));
  assign Ext_imm11 = {{5{ExtOp}}, imm11};  // Bit_Extender bit_extender_1
  assign Ext_imm5 = {{11{ExtOp}}, imm5};  // Bit_Extender bit_extender_2
  RegisterFile registerfile_1 (
    .RW(multiplexer_3_out), .RA(spliter_1_rs), .RB(spliter_1_rt), .RegWrite(RegWr), .BusW(BusW),
    .BusA(DataIn), .BusB(registerfile_1_busb));
  Multiplexer #(.width(16)) multiplexer_4 (
    .in0(registerfile_1_busb), .in1(Ext_imm11), .out(multiplexer_4_out), .sel(ALUSrc));
  ALU_circit alu_circit_1 (
    .input1(DataIn), .input2(multiplexer_4_out), .Operation(ALUOP), .functions(ALUFun),
    .ZERO({alu_circit_1_zero, Zero}));  // open: output1
  RAM #(.addrWidth(16), .dataWidth(16)) ram_1 (
    .addr(Address), .we(CrtlWE), .oe(CrtlRE), .din(DataIn), .dout(ram_1_dout));  // open: clk
  Multiplexer #(.width(16)) multiplexer_5 (.in0(ALUResult), .in1(ram_1_dout), .out(BusW), .sel(WBdata));
endmodule

module Instruction_Memory (
);

  wire PC_Ctrl;
  wire [1:0] f;
  wire [2:0] imm5;
  wire [4:0] Op;
  wire [5:0] imm11;
  wire [15:0] multiplexer_1_out, PC, PC_PLUS_2;

  Multiplexer #(.width(16)) multiplexer_1 (.in0(PC_PLUS_2), .out(multiplexer_1_out), .sel(PC_Ctrl));  // open: in1
  Adder #(.width(16)) adder_1 (.a(16'h2), .b(PC), .out(PC_PLUS_2));  // open: cin, cout
  Register #(.width(16)) InstrectionRegister_PC (.D(multiplexer_1_out), .Q(PC));  // open: en, clk, clr
  ROM #(.addrWidth(16), .dataWidth(16)) rom_1 (.addr(PC), .data({Op, f, imm5, imm11}));
  // RegisterFile registerfile_1: pin names not known; wires that end beside it: imm11[5:3], imm5

  // Other names for the same wires on the sheet: Rt[2:0] = imm11[2:0]; Rs[2:0] = imm11[5:3]; imm11[10:6] = {f, imm5};
  //   Rd[2:0] = imm5; imm5[4:3] = f
endmodule

module Spliter (
  input  [15:0] I,
  output [4:0] OpCode,
  output [10:0] imm11,
  output [2:0] Rt,
  output [2:0] Rs,
  output [2:0] Rd,
  output [1:0] f,
  output [4:0] imm5
);


  assign f = I[10:9];
  assign imm5 = I[10:6];
  assign imm11 = I[10:0];
  assign OpCode = I[15:11];
  assign Rd = I[8:6];
  assign Rs = I[5:3];
  assign Rt = I[2:0];
endmodule
